// Digital circuit Subterranean2.0.dig as structural Verilog
module Subterranean2_0 (
  input  [63:0] _0_63_2,
  input  _256_2,
  input  [63:0] _64_127_2,
  input  [63:0] _128_191_2,
  input  [63:0] _191_255_2,
  output [63:0] _0_63,
  output [63:0] _64_127,
  output [63:0] _128_191,
  output [63:0] _191_255,
  output _256
);

  wire \θ_1_p10 , \ι_1_o256 , \χ_1_p10 ;
  wire [63:0] \θ_1_p6 , \θ_1_p7 , \θ_1_p8 , \θ_1_p9 , \ι_1_o0_63 , \ι_1_o64_127 , \ι_1_o128_191 ,
       \ι_1_o192_255 , \χ_1_p6 , \χ_1_p7 , \χ_1_p8 , \χ_1_p9 ;

  // χ χ_1: pin names not known; wires that end beside it: _0_63_2, _64_127_2, _128_191_2, _191_255_2, _256_2, \χ_1_p6 , \χ_1_p7 , \χ_1_p8 , \χ_1_p9 , \χ_1_p10 
  \ι  \u_ι_1  (
    ._64_127(\χ_1_p6 ), ._128_191(\χ_1_p7 ), ._191_255(\χ_1_p8 ), ._0_63(\χ_1_p9 ), ._256(\χ_1_p10 ),
    .o0_63(\ι_1_o0_63 ), .o64_127(\ι_1_o64_127 ), .o128_191(\ι_1_o128_191 ), .o192_255(\ι_1_o192_255 ),
    .o256(\ι_1_o256 ));
  // θ θ_1: pin names not known; wires that end beside it: \ι_1_o0_63 , \ι_1_o64_127 , \ι_1_o128_191 , \ι_1_o192_255 , \ι_1_o256 , \θ_1_p6 , \θ_1_p7 , \θ_1_p8 , \θ_1_p9 , \θ_1_p10 
  \π  \u_π_1  (
    ._64_127(\θ_1_p6 ), ._128_191(\θ_1_p7 ), ._191_255(\θ_1_p8 ), ._0_63(\θ_1_p9 ), ._256(\θ_1_p10 ),
    .o0_63(_0_63), .o64_127(_64_127), .o128_191(_128_191), .o192_255(_191_255), .o256(_256));
  // Pins of 1 and 64 bits meet at _0_63
  // Pins of 1 and 64 bits meet at _64_127
  // Pins of 1 and 64 bits meet at _128_191
  // Pins of 1 and 64 bits meet at _191_255
endmodule
