// Digital circuit subterranean_absorb_keyed.dig as structural Verilog
module subterranean_absorb_keyed (
  input  [63:0] State_in_0_63,
  input  [63:0] State_in_128_191,
  input  [63:0] State_in_192_255,
  input  [63:0] State_in_64_127,
  input  State_in_256,
  input  [63:0] value_in_0_63,
  input  [63:0] value_in_64_127,
  output [63:0] State__0_63,
  output [63:0] State__64_127,
  output [63:0] State__128_191,
  output [63:0] State__192_255,
  output State__256
);

  wire subterranean_duplex_1_state__256, subterranean_duplex_2_state__256, subterranean_duplex_3_state__256,
       subterranean_duplex_4_state__256;
  wire [63:0] subterranean_duplex_1_state__0_63, subterranean_duplex_1_state__64_127,
       subterranean_duplex_1_state__128_191, subterranean_duplex_1_state__192_255,
       subterranean_duplex_2_state__0_63, subterranean_duplex_2_state__64_127,
       subterranean_duplex_2_state__128_191, subterranean_duplex_2_state__192_255,
       subterranean_duplex_3_state__0_63, subterranean_duplex_3_state__64_127,
       subterranean_duplex_3_state__128_191, subterranean_duplex_3_state__192_255,
       subterranean_duplex_4_state__0_63, subterranean_duplex_4_state__64_127,
       subterranean_duplex_4_state__128_191, subterranean_duplex_4_state__192_255;

  subterranean_duplex subterranean_duplex_1 (
    .state_0_63(State_in_0_63), .state_128_191(State_in_64_127), .state_192_255(State_in_128_191),
    .state_64_127(State_in_192_255), .state_256(State_in_256), .sigma(value_in_0_63[31:0]),
    .state__0_63(subterranean_duplex_1_state__0_63), .state__64_127(subterranean_duplex_1_state__64_127),
    .state__128_191(subterranean_duplex_1_state__128_191),
    .state__192_255(subterranean_duplex_1_state__192_255), .state__256(subterranean_duplex_1_state__256));
  subterranean_duplex subterranean_duplex_2 (
    .state_0_63(subterranean_duplex_1_state__0_63), .state_128_191(subterranean_duplex_1_state__64_127),
    .state_192_255(subterranean_duplex_1_state__128_191),
    .state_64_127(subterranean_duplex_1_state__192_255), .state_256(subterranean_duplex_1_state__256),
    .sigma(value_in_0_63[63:32]), .state__0_63(subterranean_duplex_2_state__0_63),
    .state__64_127(subterranean_duplex_2_state__64_127),
    .state__128_191(subterranean_duplex_2_state__128_191),
    .state__192_255(subterranean_duplex_2_state__192_255), .state__256(subterranean_duplex_2_state__256));
  subterranean_duplex subterranean_duplex_3 (
    .state_0_63(subterranean_duplex_2_state__0_63), .state_128_191(subterranean_duplex_2_state__64_127),
    .state_192_255(subterranean_duplex_2_state__128_191),
    .state_64_127(subterranean_duplex_2_state__192_255), .state_256(subterranean_duplex_2_state__256),
    .sigma(value_in_64_127[31:0]), .state__0_63(subterranean_duplex_3_state__0_63),
    .state__64_127(subterranean_duplex_3_state__64_127),
    .state__128_191(subterranean_duplex_3_state__128_191),
    .state__192_255(subterranean_duplex_3_state__192_255), .state__256(subterranean_duplex_3_state__256));
  subterranean_duplex subterranean_duplex_4 (
    .state_0_63(subterranean_duplex_3_state__0_63), .state_128_191(subterranean_duplex_3_state__64_127),
    .state_192_255(subterranean_duplex_3_state__128_191),
    .state_64_127(subterranean_duplex_3_state__192_255), .state_256(subterranean_duplex_3_state__256),
    .sigma(value_in_64_127[63:32]), .state__0_63(subterranean_duplex_4_state__0_63),
    .state__64_127(subterranean_duplex_4_state__64_127),
    .state__128_191(subterranean_duplex_4_state__128_191),
    .state__192_255(subterranean_duplex_4_state__192_255), .state__256(subterranean_duplex_4_state__256));
  subterranean_duplex_0bit subterranean_duplex_0bit_1 (
    .state_0_63(subterranean_duplex_4_state__0_63), .state_128_191(subterranean_duplex_4_state__64_127),
    .state_192_255(subterranean_duplex_4_state__128_191),
    .state_64_127(subterranean_duplex_4_state__192_255), .state_256(subterranean_duplex_4_state__256),
    .D0State__0_63(State__0_63), .D0State__64_127(State__64_127), .D0State__128_191(State__128_191),
    .D0State__192_255(State__192_255), .D0State__256(State__256));
endmodule
