// Digital circuit subterranean_duplex.dig as structural Verilog
module subterranean_duplex (
  input  [63:0] state_0_63,
  input  [63:0] state_128_191,
  input  [63:0] state_192_255,
  input  [63:0] state_64_127,
  input  state_256,
  input  [31:0] sigma,
  output [63:0] state__0_63,
  output [63:0] state__64_127,
  output [63:0] state__128_191,
  output [63:0] state__192_255,
  output state__256
);

  wire subterranean_round_1_o256;
  wire [35:1] subterranean_round_1_o0_63;
  wire [47:0] subterranean_round_1_o64_127;
  wire [57:5] subterranean_round_1_o191_255;
  wire [62:0] subterranean_round_1_o128_191;

  Subterranean_round subterranean_round_1 (
    ._0_63(state_0_63), ._64_127(state_64_127), ._128_191(state_128_191), ._192_255(state_192_255),
    ._256(state_256),
    .o0_63({state__0_63[63:36], subterranean_round_1_o0_63[35], state__0_63[34:31], subterranean_round_1_o0_63[30], state__0_63[29:23], subterranean_round_1_o0_63[22], state__0_63[21:18], subterranean_round_1_o0_63[17], state__0_63[16], subterranean_round_1_o0_63[15], state__0_63[14:12], subterranean_round_1_o0_63[11], state__0_63[10:5], subterranean_round_1_o0_63[4], state__0_63[3], subterranean_round_1_o0_63[2:1], state__0_63[0]}),
    .o64_127({state__64_127[63:48], subterranean_round_1_o64_127[47], state__64_127[46:32], subterranean_round_1_o64_127[31], state__64_127[30:7], subterranean_round_1_o64_127[6], state__64_127[5:1], subterranean_round_1_o64_127[0]}),
    .o128_191({state__128_191[63], subterranean_round_1_o128_191[62:61], state__128_191[60:57], subterranean_round_1_o128_191[56], state__128_191[55:49], subterranean_round_1_o128_191[48], state__128_191[47:42], subterranean_round_1_o128_191[41], state__128_191[40:38], subterranean_round_1_o128_191[37], state__128_191[36:13], subterranean_round_1_o128_191[12], state__128_191[11:10], subterranean_round_1_o128_191[9:8], state__128_191[7], subterranean_round_1_o128_191[6], state__128_191[5:1], subterranean_round_1_o128_191[0]}),
    .o191_255({state__192_255[63:58], subterranean_round_1_o191_255[57], state__192_255[56:50], subterranean_round_1_o191_255[49], state__192_255[48:43], subterranean_round_1_o191_255[42], state__192_255[41:34], subterranean_round_1_o191_255[33], state__192_255[32], subterranean_round_1_o191_255[31], state__192_255[30:22], subterranean_round_1_o191_255[21], state__192_255[20], subterranean_round_1_o191_255[19], state__192_255[18:6], subterranean_round_1_o191_255[5], state__192_255[4:0]}),
    .o256(subterranean_round_1_o256));
  xor xor_1 (state__0_63[1], subterranean_round_1_o0_63[1], sigma[0]);
  xor xor_2 (state__0_63[2], subterranean_round_1_o0_63[2], sigma[12]);
  xor xor_3 (state__0_63[4], subterranean_round_1_o0_63[4], sigma[24]);
  xor xor_4 (state__0_63[11], subterranean_round_1_o0_63[11], sigma[17]);
  xor xor_5 (state__0_63[15], subterranean_round_1_o0_63[15], sigma[14]);
  xor xor_6 (state__0_63[17], subterranean_round_1_o0_63[17], sigma[30]);
  xor xor_7 (state__0_63[22], subterranean_round_1_o0_63[22], sigma[29]);
  xor xor_8 (state__0_63[30], subterranean_round_1_o0_63[30], sigma[26]);
  xor xor_9 (state__0_63[35], subterranean_round_1_o0_63[35], sigma[3]);
  xor xor_10 (state__64_127[0], subterranean_round_1_o64_127[0], sigma[8]);
  xor xor_11 (state__64_127[6], subterranean_round_1_o64_127[6], sigma[15]);
  xor xor_12 (state__64_127[31], subterranean_round_1_o64_127[31], sigma[13]);
  xor xor_13 (state__64_127[47], subterranean_round_1_o64_127[47], sigma[23]);
  xor xor_14 (state__128_191[0], subterranean_round_1_o128_191[0], sigma[20]);
  xor xor_15 (state__128_191[6], subterranean_round_1_o128_191[6], sigma[5]);
  xor xor_16 (state__128_191[8], subterranean_round_1_o128_191[8], sigma[2]);
  xor xor_17 (state__128_191[9], subterranean_round_1_o128_191[9], sigma[18]);
  xor xor_18 (state__128_191[12], subterranean_round_1_o128_191[12], sigma[27]);
  xor xor_19 (state__128_191[37], subterranean_round_1_o128_191[37], sigma[31]);
  xor xor_20 (state__128_191[41], subterranean_round_1_o128_191[41], sigma[21]);
  xor xor_21 (state__128_191[48], subterranean_round_1_o128_191[48], sigma[1]);
  xor xor_22 (state__128_191[56], subterranean_round_1_o128_191[56], sigma[11]);
  xor xor_23 (state__128_191[61], subterranean_round_1_o128_191[61], sigma[22]);
  xor xor_24 (state__128_191[62], subterranean_round_1_o128_191[62], sigma[25]);
  xor xor_25 (state__192_255[5], subterranean_round_1_o191_255[5], sigma[6]);
  xor xor_26 (state__192_255[19], subterranean_round_1_o191_255[19], sigma[19]);
  xor xor_27 (state__192_255[21], subterranean_round_1_o191_255[21], sigma[9]);
  xor xor_28 (state__192_255[31], subterranean_round_1_o191_255[31], sigma[10]);
  xor xor_29 (state__192_255[33], subterranean_round_1_o191_255[33], sigma[28]);
  xor xor_30 (state__192_255[42], subterranean_round_1_o191_255[42], sigma[7]);
  xor xor_31 (state__192_255[49], subterranean_round_1_o191_255[49], sigma[16]);
  xor xor_32 (state__192_255[57], subterranean_round_1_o191_255[57], sigma[4]);
  xor xor_33 (state__256, 1'b1, subterranean_round_1_o256);
endmodule
