// Digital circuit subterranean_duplex_0bit.dig as structural Verilog
module subterranean_duplex_0bit (
  input  [63:0] state_0_63,
  input  [63:0] state_128_191,
  input  [63:0] state_192_255,
  input  [63:0] state_64_127,
  input  [63:0] state_256,
  output [63:0] state__0_63,
  output [63:0] state__64_127,
  output [63:0] state__128_191,
  output [63:0] state__192_255,
  output state__256
);

  wire [1:1] subterranean_round_1_p6;

  // Subterranean_round subterranean_round_1: pin names not known; wires that end beside it: state_0_63, state_64_127, state_128_191, state_192_255, state_256, {state__0_63[63:2], subterranean_round_1_p6[1], state__0_63[0]}, state__64_127, state__128_191, state__192_255, state__256
  xor xor_1 (state__0_63[1], 1'b1, subterranean_round_1_p6[1]);
endmodule
