// Digital circuit θ.dig as structural Verilog
module \θ  (
  input  [63:0] _0_63,
  input  [63:0] _64_127,
  input  [63:0] _64_128,
  input  [63:0] _128_191_2,
  input  [63:0] _191_255,
  output [63:0] _0_63_2,
  output [63:0] _128_191,
  output [63:0] _192_255,
  output [63:0] _64_127_2
);

  wire xor_193_out, xor_194_out, xor_195_out, xor_196_out, xor_197_out, xor_198_out, xor_199_out,
       xor_200_out, xor_201_out, xor_202_out, xor_203_out, xor_204_out, xor_205_out, xor_206_out,
       xor_207_out, xor_208_out, xor_209_out, xor_210_out, xor_211_out, xor_212_out, xor_213_out,
       xor_214_out, xor_215_out, xor_216_out, xor_217_out, xor_218_out, xor_219_out, xor_220_out,
       xor_221_out, xor_222_out, xor_223_out, xor_224_out;

  xor xor_1 (_0_63_2[0], _0_63[0], _0_63[3], _0_63[8]);
  xor xor_2 (_0_63_2[1], _0_63[1], _0_63[4], _0_63[9]);
  xor xor_3 (_0_63_2[2], _0_63[2], _0_63[5], _0_63[10]);
  xor xor_4 (_0_63_2[3], _0_63[3], _0_63[6], _0_63[11]);
  xor xor_5 (_0_63_2[4], _0_63[4], _0_63[7], _0_63[12]);
  xor xor_6 (_0_63_2[5], _0_63[5], _0_63[8], _0_63[13]);
  xor xor_7 (_0_63_2[6], _0_63[6], _0_63[9], _0_63[14]);
  xor xor_8 (_0_63_2[7], _0_63[7], _0_63[10], _0_63[15]);
  xor xor_9 (_0_63_2[8], _0_63[8], _0_63[11], _0_63[16]);
  xor xor_10 (_0_63_2[9], _0_63[9], _0_63[12], _0_63[17]);
  xor xor_11 (_0_63_2[10], _0_63[10], _0_63[13], _0_63[18]);
  xor xor_12 (_0_63_2[11], _0_63[11], _0_63[14], _0_63[19]);
  xor xor_13 (_0_63_2[12], _0_63[12], _0_63[15], _0_63[20]);
  xor xor_14 (_0_63_2[13], _0_63[13], _0_63[16], _0_63[21]);
  xor xor_15 (_0_63_2[14], _0_63[14], _0_63[17], _0_63[22]);
  xor xor_16 (_0_63_2[15], _0_63[15], _0_63[18], _0_63[23]);
  xor xor_17 (_0_63_2[16], _0_63[16], _0_63[19], _0_63[24]);
  xor xor_18 (_0_63_2[17], _0_63[17], _0_63[20], _0_63[25]);
  xor xor_19 (_0_63_2[18], _0_63[18], _0_63[21], _0_63[26]);
  xor xor_20 (_0_63_2[19], _0_63[19], _0_63[22], _0_63[27]);
  xor xor_21 (_0_63_2[20], _0_63[20], _0_63[23], _0_63[28]);
  xor xor_22 (_0_63_2[21], _0_63[21], _0_63[24], _0_63[29]);
  xor xor_23 (_0_63_2[22], _0_63[22], _0_63[25], _0_63[30]);
  xor xor_24 (_0_63_2[23], _0_63[23], _0_63[26], _0_63[31]);
  xor xor_25 (_0_63_2[24], _0_63[24], _0_63[27], _0_63[32]);
  xor xor_26 (_0_63_2[25], _0_63[25], _0_63[28], _0_63[33]);
  xor xor_27 (_0_63_2[26], _0_63[26], _0_63[29], _0_63[34]);
  xor xor_28 (_0_63_2[27], _0_63[27], _0_63[30], _0_63[35]);
  xor xor_29 (_0_63_2[28], _0_63[28], _0_63[31], _0_63[36]);
  xor xor_30 (_0_63_2[29], _0_63[29], _0_63[32], _0_63[37]);
  xor xor_31 (_0_63_2[30], _0_63[30], _0_63[33], _0_63[38]);
  xor xor_32 (_0_63_2[31], _0_63[31], _0_63[34], _0_63[39]);
  xor xor_33 (_0_63_2[32], _0_63[32], _0_63[35], _0_63[40]);
  xor xor_34 (_0_63_2[33], _0_63[33], _0_63[36], _0_63[41]);
  xor xor_35 (_0_63_2[34], _0_63[34], _0_63[37], _0_63[42]);
  xor xor_36 (_0_63_2[35], _0_63[35], _0_63[38], _0_63[43]);
  xor xor_37 (_0_63_2[36], _0_63[36], _0_63[39], _0_63[44]);
  xor xor_38 (_0_63_2[37], _0_63[37], _0_63[40], _0_63[45]);
  xor xor_39 (_0_63_2[38], _0_63[38], _0_63[41], _0_63[46]);
  xor xor_40 (_0_63_2[39], _0_63[39], _0_63[42], _0_63[47]);
  xor xor_41 (_0_63_2[40], _0_63[40], _0_63[43], _0_63[48]);
  xor xor_42 (_0_63_2[41], _0_63[41], _0_63[44], _0_63[49]);
  xor xor_43 (_0_63_2[42], _0_63[42], _0_63[45], _0_63[50]);
  xor xor_44 (_0_63_2[43], _0_63[43], _0_63[46], _0_63[51]);
  xor xor_45 (_0_63_2[44], _0_63[44], _0_63[47], _0_63[52]);
  xor xor_46 (_0_63_2[45], _0_63[45], _0_63[48], _0_63[53]);
  xor xor_47 (_0_63_2[46], _0_63[46], _0_63[49], _0_63[54]);
  xor xor_48 (_0_63_2[47], _0_63[47], _0_63[50], _0_63[55]);
  xor xor_49 (_0_63_2[48], _0_63[48], _0_63[51], _0_63[56]);
  xor xor_50 (_0_63_2[49], _0_63[49], _0_63[52], _0_63[57]);
  xor xor_51 (_0_63_2[50], _0_63[50], _0_63[53], _0_63[58]);
  xor xor_52 (_0_63_2[51], _0_63[51], _0_63[54], _0_63[59]);
  xor xor_53 (_0_63_2[52], _0_63[52], _0_63[55], _0_63[60]);
  xor xor_54 (_0_63_2[53], _0_63[53], _0_63[56], _0_63[61]);
  xor xor_55 (_0_63_2[54], _0_63[54], _0_63[57], _0_63[62]);
  xor xor_56 (_0_63_2[55], _0_63[55], _0_63[58], _0_63[63]);
  xor xor_57 (_0_63_2[56], _64_128[0], _64_128[3], _64_128[8]);
  xor xor_58 (_0_63_2[57], _64_128[1], _64_128[4], _64_128[9]);
  xor xor_59 (_0_63_2[58], _64_128[2], _64_128[5], _64_128[10]);
  xor xor_60 (_0_63_2[59], _64_128[3], _64_128[6], _64_128[11]);
  xor xor_61 (_0_63_2[60], _64_128[4], _64_128[7], _64_128[12]);
  xor xor_62 (_0_63_2[61], _64_128[5], _64_128[8], _64_128[13]);
  xor xor_63 (_0_63_2[62], _64_128[6], _64_128[9], _64_128[14]);
  xor xor_64 (_0_63_2[63], _64_128[7], _64_128[10], _64_128[15]);
  xor xor_65 (_64_127_2[0], _64_128[8], _64_128[11], _64_128[16]);
  xor xor_66 (_64_127_2[1], _64_128[9], _64_128[12], _64_128[17]);
  xor xor_67 (_64_127_2[2], _64_128[10], _64_128[13], _64_128[18]);
  xor xor_68 (_64_127_2[3], _64_128[11], _64_128[14], _64_128[19]);
  xor xor_69 (_64_127_2[4], _64_128[12], _64_128[15], _64_128[20]);
  xor xor_70 (_64_127_2[5], _64_128[13], _64_128[16], _64_128[21]);
  xor xor_71 (_64_127_2[6], _64_128[14], _64_128[17], _64_128[22]);
  xor xor_72 (_64_127_2[7], _64_128[15], _64_128[18], _64_128[23]);
  xor xor_73 (_64_127_2[8], _64_128[16], _64_128[19], _64_128[24]);
  xor xor_74 (_64_127_2[9], _64_128[17], _64_128[20], _64_128[25]);
  xor xor_75 (_64_127_2[10], _64_128[18], _64_128[21], _64_128[26]);
  xor xor_76 (_64_127_2[11], _64_128[19], _64_128[22], _64_128[27]);
  xor xor_77 (_64_127_2[12], _64_128[20], _64_128[23], _64_128[28]);
  xor xor_78 (_64_127_2[13], _64_128[21], _64_128[24], _64_128[29]);
  xor xor_79 (_64_127_2[14], _64_128[22], _64_128[25], _64_128[30]);
  xor xor_80 (_64_127_2[15], _64_128[23], _64_128[26], _64_128[31]);
  xor xor_81 (_64_127_2[16], _64_128[24], _64_128[27], _64_128[32]);
  xor xor_82 (_64_127_2[17], _64_128[25], _64_128[28], _64_128[33]);
  xor xor_83 (_64_127_2[18], _64_128[26], _64_128[29], _64_128[34]);
  xor xor_84 (_64_127_2[19], _64_128[27], _64_128[30], _64_128[35]);
  xor xor_85 (_64_127_2[20], _64_128[28], _64_128[31], _64_128[36]);
  xor xor_86 (_64_127_2[21], _64_128[29], _64_128[32], _64_128[37]);
  xor xor_87 (_64_127_2[22], _64_128[30], _64_128[33], _64_128[38]);
  xor xor_88 (_64_127_2[23], _64_128[31], _64_128[34], _64_128[39]);
  xor xor_89 (_64_127_2[24], _64_128[32], _64_128[35], _64_128[40]);
  xor xor_90 (_64_127_2[25], _64_128[33], _64_128[36], _64_128[41]);
  xor xor_91 (_64_127_2[26], _64_128[34], _64_128[37], _64_128[42]);
  xor xor_92 (_64_127_2[27], _64_128[35], _64_128[38], _64_128[43]);
  xor xor_93 (_64_127_2[28], _64_128[36], _64_128[39], _64_128[44]);
  xor xor_94 (_64_127_2[29], _64_128[37], _64_128[40], _64_128[45]);
  xor xor_95 (_64_127_2[30], _64_128[38], _64_128[41], _64_128[46]);
  xor xor_96 (_64_127_2[31], _64_128[39], _64_128[42], _64_128[47]);
  xor xor_97 (_64_127_2[32], _64_128[40], _64_128[43], _64_128[48]);
  xor xor_98 (_64_127_2[33], _64_128[41], _64_128[44], _64_128[49]);
  xor xor_99 (_64_127_2[34], _64_128[42], _64_128[45], _64_128[50]);
  xor xor_100 (_64_127_2[35], _64_128[43], _64_128[46], _64_128[51]);
  xor xor_101 (_64_127_2[36], _64_128[44], _64_128[47], _64_128[52]);
  xor xor_102 (_64_127_2[37], _64_128[45], _64_128[48], _64_128[53]);
  xor xor_103 (_64_127_2[38], _64_128[46], _64_128[49], _64_128[54]);
  xor xor_104 (_64_127_2[39], _64_128[47], _64_128[50], _64_128[55]);
  xor xor_105 (_64_127_2[40], _64_128[48], _64_128[51], _64_128[56]);
  xor xor_106 (_64_127_2[41], _64_128[49], _64_128[52], _64_128[57]);
  xor xor_107 (_64_127_2[42], _64_128[50], _64_128[53], _64_128[58]);
  xor xor_108 (_64_127_2[43], _64_128[51], _64_128[54], _64_128[59]);
  xor xor_109 (_64_127_2[44], _64_128[52], _64_128[55], _64_128[60]);
  xor xor_110 (_64_127_2[45], _64_128[53], _64_128[56], _64_128[61]);
  xor xor_111 (_64_127_2[46], _64_128[54], _64_128[57], _64_128[62]);
  xor xor_112 (_64_127_2[47], _64_128[55], _64_128[58], _64_128[63]);
  xor xor_113 (_64_127_2[48], _128_191_2[0], _128_191_2[3], _128_191_2[8]);
  xor xor_114 (_64_127_2[49], _128_191_2[1], _128_191_2[4], _128_191_2[9]);
  xor xor_115 (_64_127_2[50], _128_191_2[2], _128_191_2[5], _128_191_2[10]);
  xor xor_116 (_64_127_2[51], _128_191_2[3], _128_191_2[6], _128_191_2[11]);
  xor xor_117 (_64_127_2[52], _128_191_2[4], _128_191_2[7], _128_191_2[12]);
  xor xor_118 (_64_127_2[53], _128_191_2[5], _128_191_2[8], _128_191_2[13]);
  xor xor_119 (_64_127_2[54], _128_191_2[6], _128_191_2[9], _128_191_2[14]);
  xor xor_120 (_64_127_2[55], _128_191_2[7], _128_191_2[10]);  // open: In_3
  xor xor_121 (_64_127_2[56], _128_191_2[8], _128_191_2[11], _128_191_2[16]);
  xor xor_122 (_64_127_2[57], _128_191_2[9], _128_191_2[12], _128_191_2[17]);
  xor xor_123 (_64_127_2[58], _128_191_2[10], _128_191_2[13], _128_191_2[18]);
  xor xor_124 (_64_127_2[59], _128_191_2[11], _128_191_2[14], _128_191_2[19]);
  xor xor_125 (_64_127_2[60], _128_191_2[12], _128_191_2[15], _128_191_2[20]);
  xor xor_126 (_64_127_2[61], _128_191_2[13], _128_191_2[16], _128_191_2[21]);
  xor xor_127 (_64_127_2[62], _128_191_2[14], _128_191_2[17], _128_191_2[22]);
  xor xor_128 (_64_127_2[63], _128_191_2[15], _128_191_2[18], _128_191_2[23]);
  xor xor_129 (_191_255[0], _128_191_2[16], _128_191_2[19], _128_191_2[24]);
  xor xor_130 (_191_255[1], _128_191_2[17], _128_191_2[20], _128_191_2[25]);
  xor xor_131 (_191_255[2], _128_191_2[18], _128_191_2[21], _128_191_2[26]);
  xor xor_132 (_191_255[3], _128_191_2[19], _128_191_2[22], _128_191_2[27]);
  xor xor_133 (_191_255[4], _128_191_2[20], _128_191_2[23], _128_191_2[28]);
  xor xor_134 (_191_255[5], _128_191_2[21], _128_191_2[24], _128_191_2[29]);
  xor xor_135 (_191_255[6], _128_191_2[22], _128_191_2[25], _128_191_2[30]);
  xor xor_136 (_191_255[7], _128_191_2[23], _128_191_2[26], _128_191_2[31]);
  xor xor_137 (_191_255[8], _128_191_2[24], _128_191_2[27], _128_191_2[32]);
  xor xor_138 (_191_255[9], _128_191_2[25], _128_191_2[28], _128_191_2[33]);
  xor xor_139 (_191_255[10], _128_191_2[26], _128_191_2[29], _128_191_2[34]);
  xor xor_140 (_191_255[11], _128_191_2[27], _128_191_2[30], _128_191_2[35]);
  xor xor_141 (_191_255[12], _128_191_2[28], _128_191_2[31], _128_191_2[36]);
  xor xor_142 (_191_255[13], _128_191_2[29], _128_191_2[32], _128_191_2[37]);
  xor xor_143 (_191_255[14], _128_191_2[30], _128_191_2[33], _128_191_2[38]);
  xor xor_144 (_191_255[15], _128_191_2[31], _128_191_2[34], _128_191_2[39]);
  xor xor_145 (_191_255[16], _128_191_2[32], _128_191_2[35], _128_191_2[40]);
  xor xor_146 (_191_255[17], _128_191_2[33], _128_191_2[36], _128_191_2[41]);
  xor xor_147 (_191_255[18], _128_191_2[34], _128_191_2[37], _128_191_2[42]);
  xor xor_148 (_191_255[19], _128_191_2[35], _128_191_2[38], _128_191_2[43]);
  xor xor_149 (_191_255[20], _128_191_2[36], _128_191_2[39], _128_191_2[44]);
  xor xor_150 (_191_255[21], _128_191_2[37], _128_191_2[40], _128_191_2[45]);
  xor xor_151 (_191_255[22], _128_191_2[38], _128_191_2[41], _128_191_2[46]);
  xor xor_152 (_191_255[23], _128_191_2[39], _128_191_2[42], _128_191_2[47]);
  xor xor_153 (_191_255[24], _128_191_2[40], _128_191_2[43], _128_191_2[48]);
  xor xor_154 (_191_255[25], _128_191_2[41], _128_191_2[44], _128_191_2[49]);
  xor xor_155 (_191_255[26], _128_191_2[42], _128_191_2[45], _128_191_2[50]);
  xor xor_156 (_191_255[27], _128_191_2[43], _128_191_2[46], _128_191_2[51]);
  xor xor_157 (_191_255[28], _128_191_2[44], _128_191_2[47], _128_191_2[52]);
  xor xor_158 (_191_255[29], _128_191_2[45], _128_191_2[48], _128_191_2[53]);
  xor xor_159 (_191_255[30], _128_191_2[46], _128_191_2[49], _128_191_2[54]);
  xor xor_160 (_191_255[31], _128_191_2[47], _128_191_2[50], _128_191_2[55]);
  xor xor_161 (_191_255[32], _128_191_2[48], _128_191_2[51], _128_191_2[56]);
  xor xor_162 (_191_255[33], _128_191_2[49], _128_191_2[52], _128_191_2[57]);
  xor xor_163 (_191_255[34], _128_191_2[50], _128_191_2[53], _128_191_2[58]);
  xor xor_164 (_191_255[35], _128_191_2[51], _128_191_2[54], _128_191_2[59]);
  xor xor_165 (_191_255[36], _128_191_2[52], _128_191_2[55], _128_191_2[60]);
  xor xor_166 (_191_255[37], _128_191_2[53], _128_191_2[56], _128_191_2[61]);
  xor xor_167 (_191_255[38], _128_191_2[54], _128_191_2[57], _128_191_2[62]);
  xor xor_168 (_191_255[39], _128_191_2[55], _128_191_2[58], _128_191_2[63]);
  xor xor_169 (_191_255[40], _64_127[0], _64_127[3], _64_127[8]);
  xor xor_170 (_191_255[41], _64_127[1], _64_127[4], _64_127[9]);
  xor xor_171 (_191_255[42], _64_127[2], _64_127[5], _64_127[10]);
  xor xor_172 (_191_255[43], _64_127[3], _64_127[6], _64_127[11]);
  xor xor_173 (_191_255[44], _64_127[4], _64_127[7], _64_127[12]);
  xor xor_174 (_191_255[45], _64_127[5], _64_127[8], _64_127[13]);
  xor xor_175 (_191_255[46], _64_127[6], _64_127[9], _64_127[14]);
  xor xor_176 (_191_255[47], _64_127[7], _64_127[10], _64_127[15]);
  xor xor_177 (_191_255[48], _64_127[8], _64_127[11], _64_127[16]);
  xor xor_178 (_191_255[49], _64_127[9], _64_127[12], _64_127[17]);
  xor xor_179 (_191_255[50], _64_127[10], _64_127[13], _64_127[18]);
  xor xor_180 (_191_255[51], _64_127[11], _64_127[14], _64_127[19]);
  xor xor_181 (_191_255[52], _64_127[12], _64_127[15], _64_127[20]);
  xor xor_182 (_191_255[53], _64_127[13], _64_127[16], _64_127[21]);
  xor xor_183 (_191_255[54], _64_127[14], _64_127[17], _64_127[22]);
  xor xor_184 (_191_255[55], _64_127[15], _64_127[18], _64_127[23]);
  xor xor_185 (_191_255[56], _64_127[16], _64_127[19], _64_127[24]);
  xor xor_186 (_191_255[57], _64_127[17], _64_127[20], _64_127[25]);
  xor xor_187 (_191_255[58], _64_127[18], _64_127[21], _64_127[26]);
  xor xor_188 (_191_255[59], _64_127[19], _64_127[22], _64_127[27]);
  xor xor_189 (_191_255[60], _64_127[20], _64_127[23], _64_127[28]);
  xor xor_190 (_191_255[61], _64_127[21], _64_127[24], _64_127[29]);
  xor xor_191 (_191_255[62], _64_127[22], _64_127[25], _64_127[30]);
  xor xor_192 (_191_255[63], _64_127[23], _64_127[26], _64_127[31]);
  xor xor_193 (xor_193_out, _64_127[24], _64_127[27], _64_127[32]);
  xor xor_194 (xor_194_out, _64_127[25], _64_127[28], _64_127[33]);
  xor xor_195 (xor_195_out, _64_127[26], _64_127[29], _64_127[34]);
  xor xor_196 (xor_196_out, _64_127[27], _64_127[30], _64_127[35]);
  xor xor_197 (xor_197_out, _64_127[28], _64_127[31], _64_127[36]);
  xor xor_198 (xor_198_out, _64_127[29], _64_127[32], _64_127[37]);
  xor xor_199 (xor_199_out, _64_127[30], _64_127[33], _64_127[38]);
  xor xor_200 (xor_200_out, _64_127[31], _64_127[34], _64_127[39]);
  xor xor_201 (xor_201_out, _64_127[32], _64_127[35], _64_127[40]);
  xor xor_202 (xor_202_out, _64_127[33], _64_127[36], _64_127[41]);
  xor xor_203 (xor_203_out, _64_127[34], _64_127[37], _64_127[42]);
  xor xor_204 (xor_204_out, _64_127[35], _64_127[38], _64_127[43]);
  xor xor_205 (xor_205_out, _64_127[36], _64_127[39], _64_127[44]);
  xor xor_206 (xor_206_out, _64_127[37], _64_127[40], _64_127[45]);
  xor xor_207 (xor_207_out, _64_127[38], _64_127[41], _64_127[46]);
  xor xor_208 (xor_208_out, _64_127[39], _64_127[42], _64_127[47]);
  xor xor_209 (xor_209_out, _64_127[40], _64_127[43], _64_127[48]);
  xor xor_210 (xor_210_out, _64_127[41], _64_127[44], _64_127[49]);
  xor xor_211 (xor_211_out, _64_127[42], _64_127[45], _64_127[50]);
  xor xor_212 (xor_212_out, _64_127[43], _64_127[46], _64_127[51]);
  xor xor_213 (xor_213_out, _64_127[44], _64_127[47], _64_127[52]);
  xor xor_214 (xor_214_out, _64_127[45], _64_127[48], _64_127[53]);
  xor xor_215 (xor_215_out, _64_127[46], _64_127[49], _64_127[54]);
  xor xor_216 (xor_216_out, _64_127[47], _64_127[50], _64_127[55]);
  xor xor_217 (xor_217_out, _64_127[48], _64_127[51], _64_127[56]);
  xor xor_218 (xor_218_out, _64_127[49], _64_127[52], _64_127[57]);
  xor xor_219 (xor_219_out, _64_127[50], _64_127[53], _64_127[58]);
  xor xor_220 (xor_220_out, _64_127[51], _64_127[54], _64_127[59]);
  xor xor_221 (xor_221_out, _64_127[52], _64_127[55], _64_127[60]);
  xor xor_222 (xor_222_out, _64_127[53], _64_127[56], _64_127[61]);
  xor xor_223 (xor_223_out, _64_127[54], _64_127[57], _64_127[62]);
  xor xor_224 (xor_224_out, _64_127[55], _64_127[58], _64_127[63]);
endmodule
