// Digital circuit ι.dig as structural Verilog
// ι : si ← si + δi
// where δ_i = 1 if i = 0 else 1
module \ι  (
  input  [63:0] _64_127,
  input  [63:0] _128_191,
  input  [63:0] _191_255,
  input  [63:0] _0_63,
  input  _256,
  output [63:0] o0_63,
  output [63:0] o64_127,
  output [63:0] o128_191,
  output [63:0] o192_255,
  output o256
);

  xor xor_1 (o0_63[0], _0_63[0], 1'b1);

  assign o0_63[63:1] = _0_63[63:1];
  assign o64_127 = _64_127;
  assign o128_191 = _128_191;
  assign o192_255 = _191_255;
  assign o256 = _256;
endmodule
